# Fritzing sketch 01_-_Analog_example (saved by Fritzing 0.9.3b)
breadboards: 1

parts:
  LCD1 = LCD screen
  R1 = Resistor [tolerance=±5% resistance=2.2k package=THT]
  Onderdeel1 = Arduino Uno (Rev3)
  U1 = POT [package=pot_mammoth]
  R2 = Resistor [tolerance=±5% resistance=10k package=THT]
  U2 = POT [package=pot_mammoth]
  R3 = Resistor [tolerance=±5% resistance=10k package=THT]
  R4 = Photocell (LDR) [package=THT]
  R5 = Resistor [tolerance=±5% resistance=10k package=THT]
  J1 = Basic Force Sensing Resistor (FSR) [package=THT]
  R6 = Resistor [tolerance=±5% resistance=10k package=THT]

nets:
  VSS: LCD1.VSS, LCD1.R/W, LCD1.LED-, R1.Pin_1, Onderdeel1.GND, U1.E, U2.E, R4.pin_1, R6.Pin_1
  VDD: LCD1.VDD, LCD1.LED+, Onderdeel1.5V, U1.S, U2.S, R5.Pin_1, J1.pin_0
  N1: LCD1.V0, R1.Pin_0
  N2: LCD1.RS, Onderdeel1.D12/MISO
  N3: LCD1.E, Onderdeel1.D11_PWM/MOSI
  N4: LCD1.DB4, Onderdeel1.D5_PWM
  N5: LCD1.DB5, Onderdeel1.D4
  N6: LCD1.DB6, Onderdeel1.D3_PWM
  N7: LCD1.DB7, Onderdeel1.D2
  N8: Onderdeel1.A0, R2.Pin_1
  N9: Onderdeel1.A1, R3.Pin_1
  N10: Onderdeel1.A2, R4.pin_0, R5.Pin_0
  N11: Onderdeel1.A3, J1.pin_1, R6.Pin_0
  N12: U1.A, R2.Pin_0
  N13: U2.A, R3.Pin_0
