# Fritzing sketch 04_-_WS2812_example (saved by Fritzing 0.9.3b)

parts:
  Part1 = Arduino Uno (Rev3) - ICSP
  neopixel1 = Neopixel Ring 16

nets:
  N1: Part1.D2, neopixel1.IN
  5V: Part1.5V, neopixel1.VCC
  GND: Part1.GND, neopixel1.GND

custom parts:
  Neopixel Ring 16: Neopixel Ring x16
