# Fritzing sketch 06_-_HC06_Motor_example (saved by Fritzing 0.9.3b)
breadboards: 1

parts:
  S1 = H-Bridge with L298N
  Part1 = Bluetooth HC-05 Macho
  Part2 = Arduino Uno (Rev3)
  R1 = Resistor [tolerance=±5% resistance=10k package=THT]
  R2 = Resistor [tolerance=±5% resistance=10k package=THT]  # not connected
  R3 = Resistor [tolerance=±5% resistance=10k package=THT]
  R4 = Resistor [tolerance=±5% resistance=10k package=THT]
  R5 = Resistor [tolerance=±5% resistance=10k package=THT]
  R6 = Resistor [tolerance=±5% resistance=10k package=THT]
  M1 = DC Motor
  M2 = DC Motor
  VCC1 = Battery block 9V
  J1 = Basic Servo

nets:
  N1: S1.12V, VCC1.+
  GND: S1.GND, Part1.GND, Part2.GND, R1.Pin_0, R3.Pin_0, R4.Pin_0, R5.Pin_0, R6.Pin_0, VCC1.-, J1.gnd
  N2: S1.IN1, Part2.D3_PWM, R3.Pin_1
  N3: S1.IN2, Part2.D5_PWM, R4.Pin_1
  N4: S1.IN3, Part2.D6_PWM, R6.Pin_1
  N5: S1.IN4, Part2.D9_PWM, R5.Pin_1
  N6: S1.M1-01, M1.pin_2
  N7: S1.M1-02, M1.pin_1
  N8: S1.M2-01, M2.pin_2
  N9: S1.M2-02, M2.pin_1
  N10: Part1.TXD, Part2.D0/RX
  N11: Part1.RXD, Part2.D1/TX
  VCC: Part1.VCC, Part2.5V, J1.vcc
  N12: Part2.D10_PWM/SS, J1.pulse

notes:
  5V Supply

custom parts:
  H-Bridge with L298N: h-bridge
