# Fritzing sketch 07_-_UltraSoundEcho_with_AudioOut_example (saved by Fritzing 0.9.3b)
breadboards: 1

parts:
  hc-sr1 = hc-sr04
  Part1 = Arduino Uno (Rev3)
  R1 = Resistor [tolerance=±5% resistance=10k package=THT]
  R2 = Resistor [tolerance=±5% resistance=10k package=THT]
  J1 = Piezo Speaker

nets:
  VCC: hc-sr1.VCC, Part1.5V
  N1: hc-sr1.Trig, Part1.D4, R2.Pin_0
  N2: hc-sr1.Echo, Part1.D3_PWM, R1.Pin_0
  GND: hc-sr1.GND, Part1.GND, R1.Pin_1, R2.Pin_1, J1.pin1
  N3: Part1.D5_PWM, J1.pin2
